// Logisim project ac01.circ as structural Verilog
module memRAMq2 (
  input  [4:0] in_1,
  input  in_2,
  input  in_3,
  input  [23:0] in_4,
  input  in_5,
  output [23:0] out_6
);

  RAM #(.addrWidth(5), .dataWidth(24)) ram_1 (.addr(in_1), .we(in_2), .oe(in_3), .clk(in_5), .din(in_4), .dout(out_6));

  // Notes on the sheet:
  //   a) 5
  //   b) Os valores foram reiniciados para 0
  //   c) Sim
  //   d) Cada endereço agora possui mais 12 bits de informaçao
  //   e) A propriedade determina se eh possivel a leitura/ escrita na RAM sem que haja sinal de clock
endmodule

module memROMq1 (
  input  [4:0] in_1,
  output [11:0] out_2
);

  ROM #(.addrWidth(5), .dataWidth(12)) rom_1 (.addr(in_1), .data(out_2));

  // Notes on the sheet:
  //   c) Permanecem
  //   a) 12 * 32 = 384 bits
  //   contents of rom_1 (hex, n*v repeats v):
  //   363 3d6 74 5 5 f 898 55 e4 e 0 46 a 54f a3 3 f3 33 536 57d e 98e 54 0 3 8 689 68 a 898 745 a
endmodule

module memRAMq3 (
  input  [6:0] in_1,
  input  [7:0] in_2,
  input  in_3,
  input  [6:0] in_4,
  output [3:0] MaisSignificativa,
  output [7:0] out_6,
  output [3:0] MenosSiginificativa
);

  RAM #(.addrWidth(7), .dataWidth(4)) ram_1 (.addr(in_1), .clk(in_3), .dout(MaisSignificativa));  // open: we, oe, din
  RAM #(.addrWidth(7), .dataWidth(4)) ram_2 (.addr(in_4), .clk(in_3), .dout(MenosSiginificativa));  // open: we, oe, din
  RAM ram_3 (.addr(in_2), .clk(in_3), .dout(out_6));  // open: we, oe, din
endmodule

module memRAMq4 (
  input  in_1,
  input  [2:0] addr,
  input  [3:0] Escrita,
  output [3:0] Leitura
);

  wire clock_1_out, not_1_out;
  wire [3:0] controlled_buffer_2_out, d_ff_25_q, d_ff_26_q, d_ff_27_q, d_ff_28_q, d_ff_29_q, d_ff_30_q,
       d_ff_31_q, d_ff_32_q, demultiplexer_1_out0, demultiplexer_1_out1, demultiplexer_1_out2,
       demultiplexer_1_out3, demultiplexer_1_out4, demultiplexer_1_out5, demultiplexer_1_out6,
       demultiplexer_1_out7, multiplexer_1_out;

  assign Leitura = in_1 ? multiplexer_1_out : 4'bz;  // Controlled_Buffer controlled_buffer_1
  Multiplexer #(.select(3), .width(4)) multiplexer_1 (
    .in0(d_ff_25_q), .in1(d_ff_26_q), .in2(d_ff_27_q), .in3(d_ff_28_q), .in4(d_ff_29_q), .in5(d_ff_30_q),
    .in6(d_ff_31_q), .in7(d_ff_32_q), .out(multiplexer_1_out), .sel(addr));
  Clock clock_1 (.out(clock_1_out));
  D_Flip_Flop d_ff_1 (.D(demultiplexer_1_out0[3]), .clk(clock_1_out), .Q(d_ff_25_q[3]));  // open: Qn, preset, reset
  D_Flip_Flop d_ff_2 (.D(demultiplexer_1_out1[3]), .clk(clock_1_out), .Q(d_ff_26_q[3]));  // open: Qn, preset, reset
  D_Flip_Flop d_ff_3 (.D(demultiplexer_1_out2[3]), .clk(clock_1_out), .Q(d_ff_27_q[3]));  // open: Qn, preset, reset
  D_Flip_Flop d_ff_4 (.D(demultiplexer_1_out3[3]), .clk(clock_1_out), .Q(d_ff_28_q[3]));  // open: Qn, preset, reset
  D_Flip_Flop d_ff_5 (.D(demultiplexer_1_out4[3]), .clk(clock_1_out), .Q(d_ff_29_q[3]));  // open: Qn, preset, reset
  D_Flip_Flop d_ff_6 (.D(demultiplexer_1_out5[3]), .clk(clock_1_out), .Q(d_ff_30_q[3]));  // open: Qn, preset, reset
  D_Flip_Flop d_ff_7 (.D(demultiplexer_1_out6[3]), .clk(clock_1_out), .Q(d_ff_31_q[3]));  // open: Qn, preset, reset
  D_Flip_Flop d_ff_8 (.D(demultiplexer_1_out7[3]), .clk(clock_1_out), .Q(d_ff_32_q[3]));  // open: Qn, preset, reset
  D_Flip_Flop d_ff_9 (.D(demultiplexer_1_out0[2]), .clk(clock_1_out), .Q(d_ff_25_q[2]));  // open: Qn, preset, reset
  D_Flip_Flop d_ff_10 (.D(demultiplexer_1_out1[2]), .clk(clock_1_out), .Q(d_ff_26_q[2]));  // open: Qn, preset, reset
  D_Flip_Flop d_ff_11 (.D(demultiplexer_1_out2[2]), .clk(clock_1_out), .Q(d_ff_27_q[2]));  // open: Qn, preset, reset
  D_Flip_Flop d_ff_12 (.D(demultiplexer_1_out3[2]), .clk(clock_1_out), .Q(d_ff_28_q[2]));  // open: Qn, preset, reset
  D_Flip_Flop d_ff_13 (.D(demultiplexer_1_out4[2]), .clk(clock_1_out), .Q(d_ff_29_q[2]));  // open: Qn, preset, reset
  D_Flip_Flop d_ff_14 (.D(demultiplexer_1_out5[2]), .clk(clock_1_out), .Q(d_ff_30_q[2]));  // open: Qn, preset, reset
  D_Flip_Flop d_ff_15 (.D(demultiplexer_1_out6[2]), .clk(clock_1_out), .Q(d_ff_31_q[2]));  // open: Qn, preset, reset
  D_Flip_Flop d_ff_16 (.D(demultiplexer_1_out7[2]), .clk(clock_1_out), .Q(d_ff_32_q[2]));  // open: Qn, preset, reset
  not not_1 (not_1_out, in_1);
  D_Flip_Flop d_ff_17 (.D(demultiplexer_1_out0[1]), .clk(clock_1_out), .Q(d_ff_25_q[1]));  // open: Qn, preset, reset
  D_Flip_Flop d_ff_18 (.D(demultiplexer_1_out1[1]), .clk(clock_1_out), .Q(d_ff_26_q[1]));  // open: Qn, preset, reset
  D_Flip_Flop d_ff_19 (.D(demultiplexer_1_out2[1]), .clk(clock_1_out), .Q(d_ff_27_q[1]));  // open: Qn, preset, reset
  D_Flip_Flop d_ff_20 (.D(demultiplexer_1_out3[1]), .clk(clock_1_out), .Q(d_ff_28_q[1]));  // open: Qn, preset, reset
  D_Flip_Flop d_ff_21 (.D(demultiplexer_1_out4[1]), .clk(clock_1_out), .Q(d_ff_29_q[1]));  // open: Qn, preset, reset
  D_Flip_Flop d_ff_22 (.D(demultiplexer_1_out5[1]), .clk(clock_1_out), .Q(d_ff_30_q[1]));  // open: Qn, preset, reset
  D_Flip_Flop d_ff_23 (.D(demultiplexer_1_out6[1]), .clk(clock_1_out), .Q(d_ff_31_q[1]));  // open: Qn, preset, reset
  D_Flip_Flop d_ff_24 (.D(demultiplexer_1_out7[1]), .clk(clock_1_out), .Q(d_ff_32_q[1]));  // open: Qn, preset, reset
  D_Flip_Flop d_ff_25 (.D(demultiplexer_1_out0[0]), .clk(clock_1_out), .Q(d_ff_25_q[0]));  // open: Qn, preset, reset
  D_Flip_Flop d_ff_26 (.D(demultiplexer_1_out1[0]), .clk(clock_1_out), .Q(d_ff_26_q[0]));  // open: Qn, preset, reset
  D_Flip_Flop d_ff_27 (.D(demultiplexer_1_out2[0]), .clk(clock_1_out), .Q(d_ff_27_q[0]));  // open: Qn, preset, reset
  D_Flip_Flop d_ff_28 (.D(demultiplexer_1_out3[0]), .clk(clock_1_out), .Q(d_ff_28_q[0]));  // open: Qn, preset, reset
  D_Flip_Flop d_ff_29 (.D(demultiplexer_1_out4[0]), .clk(clock_1_out), .Q(d_ff_29_q[0]));  // open: Qn, preset, reset
  D_Flip_Flop d_ff_30 (.D(demultiplexer_1_out5[0]), .clk(clock_1_out), .Q(d_ff_30_q[0]));  // open: Qn, preset, reset
  D_Flip_Flop d_ff_31 (.D(demultiplexer_1_out6[0]), .clk(clock_1_out), .Q(d_ff_31_q[0]));  // open: Qn, preset, reset
  D_Flip_Flop d_ff_32 (.D(demultiplexer_1_out7[0]), .clk(clock_1_out), .Q(d_ff_32_q[0]));  // open: Qn, preset, reset
  Demultiplexer #(.select(3), .width(4)) demultiplexer_1 (
    .out0(demultiplexer_1_out0), .out1(demultiplexer_1_out1), .out2(demultiplexer_1_out2),
    .out3(demultiplexer_1_out3), .out4(demultiplexer_1_out4), .out5(demultiplexer_1_out5),
    .out6(demultiplexer_1_out6), .out7(demultiplexer_1_out7), .in(controlled_buffer_2_out), .sel(addr));
  assign controlled_buffer_2_out = not_1_out ? Escrita : 4'bz;  // Controlled_Buffer controlled_buffer_2
endmodule

module memROMq5 (
  input  in_1,
  input  [2:0] in_2
);

  wire decoder_1_out0, or_1_out;

  Decoder #(.select(3)) decoder_1 (
    .out0(decoder_1_out0), .sel(in_2), .en(in_1));  // open: out1, out2, out3, out4, out5, out6, out7
  buf or_1 (or_1_out, decoder_1_out0);  // OR_Gate
  memRAMq4 memramq4_1 ();  // open: in_1, addr, Escrita, Leitura

  // Notes on the sheet:
  //   3, 9, A, 7, F, 0, 2 e D.
endmodule
